# Fritzing sketch MHZ19b_CC1101_ESP32_Schematics_Fritzing_22020608 (saved by Fritzing 0.9.9b)
breadboards: 2

parts:
  U1 = ESP32S-HiLetgo [part_number=ESP32S-HiLetgo]
  TD-er1 = MH-Z19 CO2 sensor [part_number=MH-Z19]
  LED1 = smd LED [color="Red (633nm)" package="0603 [SMD]"]
  R1 = Resistor [tolerance=±5% resistance=220 package="2512 [SMD]"]
  U2 = CC1101 [part_number=CC1101]

nets:
  N1: U1.3.3, U2.1
  N2: U1.GPIO14, U2.6
  N3: U1.GPIO12, R1.Pin_0
  N4: U1.GND, LED1.cathode, U2.2
  N5: U1.GPIO2, U2.7
  N6: U1.GPIO16, TD-er1.TX
  N7: U1.GPIO17, TD-er1.RX
  N8: U1.GPIO5, U2.8
  N9: U1.GPIO18, U2.4
  N10: U1.GPIO19, U2.5
  N11: U1.GPIO23, U2.3
  N12: LED1.anode, R1.Pin_1

custom parts:
  ESP32S-HiLetgo: HiLetgo ESP-WROOM-32 ESP32 ESP-32S Development Board 2.4GHz Dual-Mode WiFi + Bluetooth Dual Cores Microcontroller The ESP32 integrated with Antenna switches, RF Balun, power amplifiers, low-noise amplifiers, filters, and management modules, and the entire solution occupies the least area of PCB. 2.4 GHz Wi-Fi plus Bluetooth dual-mode chip, with TSMC Ultra-low power consumption 40nm technology,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
